# Fritzing sketch Alarm SMS (saved by Fritzing 0.9.3b)
breadboards: 1

parts:
  ARDUINO_NANO = Arduino Nano (Rev3.0)
  LED_RGB = RGB LED (com. cathode, rgb) [package="5 mm [THT]"]
  LED_POWER_STATE = LED - 5mm [color="Red (633nm)" package="5 mm [THT]"]
  SIM = SIM800L [package=THT]
  PIR1 = MLX90614 [package=to-39]
  PIR2 = MLX90614 [package=to-39]
  PIEZO = Piezo Speaker
  12V_BUZZ = Piezo Speaker
  12V_BATT = Battery Holders [package=battcon_12mm_pth]
  220AC_to_12VDC = Transformer [package=transformer]
  B_TEST = SWITCH-MOMENTARY-2 [package=tactile-pth-12mm]
  R1 = Resistor [tolerance=±5% resistance=220 package=THT]
  R2 = Resistor [tolerance=±5% resistance=220 package=THT]
  CHARGE_CONTROL = Unproven! [package=msop-10]
  GENERAL_ON/OFF = SWITCH-DPDT [package=os]
  OPTO_220V = RELAY-SOLIDSTATE [package=relay-s108t02]
  R4 = Resistor [tolerance=±5% resistance=220 package=THT]
  Q1 = PNP-Transistor [package="TO92 [THT]"]
  R5 = Resistor [tolerance=±5% resistance=2.2k package=THT]
  R7 = Resistor [tolerance=±5% resistance=100k package=THT]
  R8 = Resistor [tolerance=±5% resistance=100k package=THT]
  R9 = Resistor [tolerance=±5% resistance=10k package=THT]
  R10 = Resistor [tolerance=±5% resistance=10k package=THT]
  R11 = Resistor [tolerance=±5% resistance=15k package=THT]
  R12 = Resistor [tolerance=±5% resistance=10k package=THT]
  B_LIGHT = Pushbutton [package=THT]
  LED_INT = LED - 5mm [color="Blue (525nm)" package="5 mm [THT]"]
  12VDC_to_5VDC = LMZ14203 [package=to-pmod-7]

nets:
  GND: ARDUINO_NANO.GND, SIM.GND, PIEZO.pin2, B_TEST.2, R1.Pin_1, R2.Pin_1, R12.Pin_1
  N1: ARDUINO_NANO.D2, B_TEST.1
  N2: ARDUINO_NANO.D3, PIEZO.pin1
  N3: ARDUINO_NANO.D6, R11.Pin_1, R12.Pin_0
  N4: ARDUINO_NANO.D7, SIM.SIM_RXD
  N5: ARDUINO_NANO.D8, SIM.SIM_TXD
  N6: ARDUINO_NANO.D9, OPTO_220V.+
  N7: ARDUINO_NANO.D10, R5.Pin_0
  N8: ARDUINO_NANO.D11/MOSI, LED_POWER_STATE.anode
  N9: ARDUINO_NANO.D12/MISO, LED_RGB.red_anode
  5V: ARDUINO_NANO.5V, SIM.5V, PIR1.VDD, PIR2.VDD, 12VDC_to_5VDC.VOUT
  N10: ARDUINO_NANO.A3, R8.Pin_1, R9.Pin_0
  N11: ARDUINO_NANO.A2, R7.Pin_1, R10.Pin_0
  N12: ARDUINO_NANO.A1, PIR2.PWM_SDA
  N13: ARDUINO_NANO.A0, PIR1.PWM_SDA
  N14: ARDUINO_NANO.D13/SCK, LED_RGB.green_anode
  VSS: PIR1.VSS, PIR2.VSS, 12V_BATT.-, 220AC_to_12VDC.2, CHARGE_CONTROL.VSS, 12VDC_to_5VDC.GND
  N15: 12V_BUZZ.pin1, CHARGE_CONTROL.PROG, B_LIGHT.leg1, LED_INT.anode, 12VDC_to_5VDC.VIN
  N16: 12V_BUZZ.pin2, Q1.E
  N17: 12V_BATT.+, GENERAL_ON/OFF.4, R7.Pin_0
  220VAC/Prise 220V: 220AC_to_12VDC.1, 220AC_to_12VDC.4, OPTO_220V.T1, OPTO_220V.T2
  N18: 220AC_to_12VDC.3, GENERAL_ON/OFF.2
  N19: CHARGE_CONTROL.VDD, GENERAL_ON/OFF.1, R8.Pin_0
  N20: CHARGE_CONTROL.VBAT, GENERAL_ON/OFF.5
  N21: OPTO_220V.-, R4.Pin_1
  GND_2: R4.Pin_0, Q1.C, R9.Pin_1, R10.Pin_1, LED_INT.cathode
  N22: Q1.B, R5.Pin_1
  N23: R11.Pin_0, B_LIGHT.leg0

// code stored in the sketch: Alarm_sms.ino
#include <Timer.h>
#include <gprs.h>
#include <softwareserial.h>

#define TIMEOUT    5000

Timer t;
Timer p;
Timer l1;
Timer l2;

boolean sms_activate;
char sms_number = "+33624944955";
char incoming_num = "+33624944955";
GPRS gprs;

const int led_R = 12;
const int led_G = 13;
const int led_B = 11;

const int pir1_pin = A0;
const int pir2_pin = A1;
int pir1_state = LOW;
int pir2_state = LOW;
unsigned count_move;
unsigned count_still;

int Alarm_State = 0;
int temporisation;
const int piezo_pin = 2;
const int B_test = 3;
const int B_light = 6;
const int relay_pin = 9;
const int buzz_pin = 10;

// POWER SUPPLY
int sms_power = 0;
const int BATT_input = A2;
const int SECT_input = A3;
int Bout = 0.0;
int Bin = 0.0;
int BATT_value = 0;
int Sout = 0.0;
int Sin = 0.0;
int SECT_value = 0;
int R1 = 100000;     // resistance of R1 (100K)
int R2 = 10000;      // resistance of R2 (10K)


void setup() {
  pinMode(led_R, OUTPUT);
  pinMode(led_G, OUTPUT);
  pinMode(led_B, OUTPUT);
  pinMode(piezo_pin, OUTPUT);
  pinMode(relay_pin, OUTPUT);
  pinMode(buzz_pin, OUTPUT);

  pinMode(pir1_pin, INPUT);
  pinMode(pir2_pin, INPUT);
  pinMode(B_test, INPUT_PULLUP);
  pinMode(B_light, INPUT_PULLUP);
  pinMode(BATT_input, INPUT);
  pinMode(SECT_input, INPUT);

  p.every(2000, checkPIR);

  //Serial.begin(9600);
  //while (!Serial);

  //Serial.println("Starting SIM800 SMS Command Processor");
  gprs.preInit();
  delay(1000);

  while (0 != gprs.init()) {
    delay(1000);
    //Serial.print("init error\r\n");
  }

  //Set SMS mode to ASCII
  if (0 != gprs.sendCmdAndWaitForResp("AT+CMGF=1\r\n", "OK", TIMEOUT)) {
    ERROR("ERROR:CNMI");
    return;
  }

  //Start listening to New SMS Message Indications
  if (0 != gprs.sendCmdAndWaitForResp("AT+CNMI=1,2,0,0,0\r\n", "OK", TIMEOUT)) {
    ERROR("ERROR:CNMI");
    return;
  }

  //Serial.println("Init success");
  //Serial.println("Alarm : Standby...");

  delay(500);
  tone(piezo_pin, 1000, 100);
  delay(200);
  tone(piezo_pin, 1000, 100);
  delay(1000);
  gprs.sendSMS (sms_number, "Alarm : Standby...");
}


//Variable to hold last line of serial output from SIM800
char currentLine[80] = "";
int currentLineIndex = 0;

//Boolean to be set to true if message notificaion was found and next
//line of serial output is the actual SMS message content
bool nextLineIsMessage = false;


void loop() {

  read_sms();
  power_check();
  Ext_light();

  if (digitalRead (B_test) == LOW) {
    digitalWrite(buzz_pin, HIGH);
    delay(200);
    digitalWrite(buzz_pin, LOW);
    digitalWrite(relay_pin, HIGH);
    delay(500);
    digitalWrite(relay_pin, LOW);
    sms_activate = !sms_activate;
  }

  if (sms_activate == 1 && Alarm_State == 0) {
    delay(1000);
    //Serial.println("temporisation... ");
    tone(piezo_pin, 500, 100);
    Alarm_State = 3;
    int temporisation = t.after(20000, Alarm_ON);
  }
  if (sms_activate == 0 && Alarm_State != 0) {
    delay(1000);
    //Serial.println("Alarm : OFF");
    tone(piezo_pin, 500, 100);
    t.stop(temporisation);
    Alarm_State = 0;
    gprs.sendSMS (sms_number, "Alarm : OFF");
    if (incoming_num != sms_number) {
      gprs.sendSMS (incoming_num, "Alarm : OFF");
      delay(1000);
      incoming_num = sms_number;
    }
  }

  switch (Alarm_State) {
    case 0:
      digitalWrite(led_R, LOW);
      digitalWrite(led_G, HIGH);
      digitalWrite(buzz_pin, LOW);
      count_move = 0;
      count_still = 0;
      break;
    case 1:
      digitalWrite(led_R, HIGH);
      digitalWrite(led_G, LOW);
      digitalWrite(buzz_pin, LOW);
      p.update();
      break;
    case 3:
      //digitalWrite(led_R, LOW);
      //digitalWrite(led_G, LOW);
      t.update();
      l1.oscillate(led_G, 500, HIGH);
      l1.update();
      break;
    case 4:
      //digitalWrite(led_R, LOW);
      //digitalWrite(led_G, LOW);
      //tone(piezo_pin, 2000, 100);
      //delay(200);
      digitalWrite(buzz_pin, HIGH);
      p.update();
      l1.oscillate(led_R, 250, HIGH);
      l1.update();
      l2.oscillate(relay_pin, 500, HIGH);
      l2.update();
      break;
  }
}


int Alarm_ON() {
  Alarm_State = 1;
  //Serial.println("Alarm : ON");
  tone(piezo_pin, 2000, 1000);
  delay(1000);
  gprs.sendSMS (sms_number, "Alarm : ON");
  if (incoming_num != sms_number) {
    gprs.sendSMS (incoming_num, "Alarm : OFF");
    delay(1000);
    incoming_num = sms_number;
  }
}


int checkPIR() {

  pir1_state = digitalRead(pir1_pin);
  if (pir1_state == HIGH && Alarm_State == 1) {
    count_move ++;
  }
  pir2_state = digitalRead(pir2_pin);
  if (pir2_state == HIGH && Alarm_State == 1) {
    count_move ++;
  }

  //PIR detection//
  if (count_move == 1) {
    count_still = 0;
    tone(piezo_pin, 2000, 2000);
  }

  if (Alarm_State == 1) {
    count_still ++;
    if (count_still > 10) {
      count_move = 0;
      count_still = 0;
    }
  }

  if (count_move >= 9) {
    count_move = 0;
    count_still = 0;
    Alarm_State = 4;
    gprs.sendSMS (sms_number, "Alarm : ALERT !!!");
  }

  if (Alarm_State == 4) {
    count_still ++;
    if (count_still > 30) {
      count_move = 0;
      count_still = 0;
      Alarm_State = 1;
    }
  }
  /*Serial.print("count_still : ");
    Serial.print(count_still);
    Serial.print(" // count_move : ");
    Serial.println(count_move);*/
}


void read_sms() {

  //If there is serial output from SIM800
  if (gprs.serialSIM800.available()) {
    char lastCharRead = gprs.serialSIM800.read();
    //Read each character from serial output until \r or \n is reached (which denotes end of line)
    if (lastCharRead == '\r' || lastCharRead == '\n') {
      String lastLine = String(currentLine);

      //If last line read +CMT, New SMS Message Indications was received.
      //Hence, next line is the message content.
      if (lastLine.startsWith("+CMT:")) {

        //Serial.println(lastLine);
        nextLineIsMessage = true;

        if (lastLine.indexOf("+33") >= 0) {
          //Serial.println(lastLine.substring(6, 18));
          //char copy[12];
          lastLine.substring(6, 18).toCharArray(incoming_num, 12);
          //incoming_num = copy;
        }

      } else if (lastLine.length() > 0) {

        if (nextLineIsMessage) {
          //Serial.println(lastLine);

          //Read message content and set status according to SMS content
          if (lastLine.indexOf("ON") >= 0) {
            sms_activate = 1;
          } else if (lastLine.indexOf("OFF") >= 0) {
            sms_activate = 0;
          } else if (lastLine.indexOf("Statut") >= 0) {
            if (Alarm_State == 0) {
              gprs.sendSMS (sms_number, "Alarm : OFF");
            } else if (Alarm_State == 1) {
              gprs.sendSMS (sms_number, "Alarm : ON");
            } else if (Alarm_State == 4) {
              gprs.sendSMS (sms_number, "Alarm : ALERT !!!");
            }
          } else if (lastLine.indexOf("Power") >= 0) {
            gprs.sendSMS (sms_number, "Power states (Sector/Battery)");
            gprs.sendSMS (sms_number, Sin);
            gprs.sendSMS (sms_number, Bin);
            sms_power = 0;
          }

          nextLineIsMessage = false;
        }

      }

      //Clear char array for next line of read
      for ( int i = 0; i < sizeof(currentLine);  ++i ) {
        currentLine[i] = (char)0;
      }
      currentLineIndex = 0;
    } else {
      currentLine[currentLineIndex++] = lastCharRead;
    }
  }
}


void power_check() {

  BATT_value = analogRead(BATT_input);
  SECT_value = analogRead(SECT_input);

  Bout = (BATT_value * 5.0) / 1024.0;
  Bin = Bout / (R2 / (R1 + R2));
  Sout = (SECT_value * 5.0) / 1024.0;
  Sin = Sout / (R2 / (R1 + R2));

  //Serial.print("Power values : BATT = ");
  //Serial.print(Bin);
  //Serial.print(" // SECT = ");
  //Serial.print(Sin);

  if (sms_power == 0) {
    if (Sin <= 1 && Bin >= 10) {
      digitalWrite(led_B, HIGH);
      //Serial.println("Power Down! Battery Ok.");
      gprs.sendSMS (sms_number, "Power Down! Battery Ok.");
      sms_power = 1;
    }
  }
  if (sms_power <= 1) {
    if (Sin <= 1 && Bin < 10) {
      digitalWrite(led_B, HIGH);
      //Serial.println("Battery Low!");
      gprs.sendSMS (sms_number, "Battery Low!");
      sms_power = 2;
    }
  }
}

int Ext_light() {
  if (digitalRead(B_light) == HIGH && Alarm_State == 0) {
    digitalWrite(relay_pin, HIGH);
  } else {
    digitalWrite(relay_pin, LOW);
  }
}
